# Fritzing sketch common-collector-1-fritz (saved by Fritzing 0.9.3b)
breadboards: 1

parts:
  R1 = Resistor [tolerance=±5% resistance=200k package=THT]
  R3 = Resistor [tolerance=±5% resistance=3.9k package=THT]
  Q1 = NPN-Transistor [package="TO92 [THT]"]
  VCC1 = Battery
  S1 = Pushbutton [package="[THT]"]
  Q2 = Basic FET N-Channel [package="TO220 [THT]"]
  L1 = Solenoid
  D1 = Rectifier Diode [part_number=1N4001 package="300 mil [THT]"]

nets:
  N1: R1.Pin_0, Q1.E, Q2.gate
  N2: R1.Pin_1, VCC1.-, Q2.source
  N3: R3.Pin_0, Q1.C, VCC1.+
  N4: R3.Pin_1, S1.Pin_1, S1.Pin_2
  N5: Q1.B, S1.Pin_3, S1.Pin_4
  N6: Q2.drain, L1.pin1, D1.anode
  N7: L1.pin2, D1.cathode

notes:
  [TO BIG BATTERY]
