# Fritzing sketch common-emitter-1-fritz (saved by Fritzing 0.9.3b)
breadboards: 1

parts:
  R1 = Resistor [tolerance=±5% resistance=100k package=THT]
  R2 = Trimmer Potentiometer [maximum_resistance=10kΩ package=THT]
  R3 = Resistor [tolerance=±5% resistance=10k package=THT]
  Q1 = NPN-Transistor [package="TO92 [THT]"]
  VCC1 = Battery

nets:
  N1: R1.Pin_0, Q1.B
  N2: R2.leg1, R2.wiper, Q1.E, VCC1.-
  N3: R2.leg2, R3.Pin_1, VCC1.+
  N4: R3.Pin_0, Q1.C

notes:
  [GROUND]
  [Test Point 1
  Base Voltage]
  [Test Point 2
  Collector Voltage]
