# Fritzing sketch fet-1-fritz (saved by Fritzing 0.9.3b)
breadboards: 1

parts:
  R1 = Resistor [tolerance=±5% resistance=100k package=THT]
  R2 = Trimmer Potentiometer [maximum_resistance=10kΩ package=THT]
  Q1 = NPN-Transistor [package="TO92 [THT]"]
  LED1 = LED - 5mm [color="Red (633nm)" package="5 mm [THT]"]
  R3 = Resistor [tolerance=±5% resistance=510 package=THT]
  VCC1 = 4 x AAA Battery Mount
  FET1 = STP16NF06 N-Channel Power MOSFET
  L1 = Solenoid
  R4 = Resistor [tolerance=±5% resistance=10k package=THT]
  D1 = Rectifier Diode [part_number=1N4001 package="300 mil [THT]"]
  R5 = Resistor [tolerance=±5% resistance=100 package=THT]

nets:
  N1: R1.Pin_0, Q1.B
  N2: R2.leg1, R2.wiper, LED1.cathode, VCC1.-, R4.Pin_0
  N3: R2.leg2, VCC1.+
  N4: Q1.E, R4.Pin_1, R5.Pin_0
  N5: LED1.anode, R3.Pin_1
  N6: R3.Pin_0, FET1.source
  N7: FET1.gate, R5.Pin_1
  N8: FET1.drain, L1.pin1, D1.anode
  N9: L1.pin2, D1.cathode

notes:
  [GROUND]
  [Test Point 1
  Base Voltage]
  [Test Point 2
  Collector Voltage]
  To fuse-protected battery

custom parts:
  STP16NF06 N-Channel Power MOSFET: STP16NF06 N-channel Power MOSFET
